# Fritzing sketch High Level Controller (saved by Fritzing 0.8.7b)
breadboards: 1

parts:
  Part1 = Arduino Nano (Rev3.0)
  Power_plug1 = Power plug
  IC1 = IC, DIP package, 16 pins [chip_label=ULN2069B]
  IC2 = IC, DIP package, 16 pins [chip_label=ULN2069B part_number=ULN2069B]
  D1 = Schottky Diode [part_number=1N5817 package="300 mil [THT]"]
  D2 = Schottky Diode [part_number=1N5817 package="300 mil [THT]"]
  D3 = Schottky Diode [part_number=1N5817 package="300 mil [THT]"]
  D4 = Schottky Diode [part_number=1N5817 package="300 mil [THT]"]
  D5 = Schottky Diode [part_number=1N5817 package="300 mil [THT]"]  # not connected
  D6 = Schottky Diode [part_number=1N5817 package="300 mil [THT]"]  # not connected
  D7 = Schottky Diode [part_number=1N5817 package="300 mil [THT]"]
  D8 = Schottky Diode [part_number=1N5817 package="300 mil [THT]"]
  C1 = Ceramic Capacitor [capacitance=100nF package="100 mil [THT, multilayer]"]
  C2 = Ceramic Capacitor [capacitance=100nF package="100 mil [THT, multilayer]"]
  C3 = Ceramic Capacitor [capacitance=100nF package="100 mil [THT, multilayer]"]
  C4 = Ceramic Capacitor [capacitance=100nF package="100 mil [THT, multilayer]"]
  C5 = Ceramic Capacitor [capacitance=100nF package="100 mil [THT, multilayer]"]
  C6 = Ceramic Capacitor [capacitance=100nF package="100 mil [THT, multilayer]"]
  C7 = Ceramic Capacitor [capacitance=100nF package="100 mil [THT, multilayer]"]
  C8 = Ceramic Capacitor [capacitance=100nF package="100 mil [THT, multilayer]"]

nets:
  GND: Part1.GND, Power_plug1.GND, IC1.pin4, IC1.pin5, IC1.pin12, IC1.pin13, IC2.pin4, IC2.pin5, IC2.pin12, IC2.pin13, IC2.pin14
  N1: Part1.D9, IC2.pin3
  N2: Part1.D10, IC2.pin6
  N3: Part1.D11/MOSI, IC1.pin3
  N4: Part1.D12/MISO, IC1.pin6
  VIN: Part1.VIN, Power_plug1.VCC, IC1.pin14, D1.cathode, D2.cathode, D3.cathode, D4.cathode, D7.cathode, D8.cathode, C1.0, C2.0, C3.0, C4.0, C5.1, C6.1, C7.1, C8.1
  N5: Part1.A0, IC2.pin15
  N6: Part1.AREF, IC2.pin11
  N7: Part1.3V3, IC1.pin11
  N8: Part1.D13/SCK, IC1.pin15
  N9: IC1.pin2, D7.anode, C2.1
  N10: IC1.pin8, D8.anode, C1.1
  N11: IC1.pin10, D4.anode, C8.0
  N12: IC1.pin16, D3.anode, C7.0
  N13: IC2.pin2, C4.1
  N14: IC2.pin8, C3.1
  N15: IC2.pin10, D2.anode, C6.0
  N16: IC2.pin16, D1.anode, C5.0
