# Fritzing sketch Motor Driver Arduino (saved by Fritzing 0.8.7b)
breadboards: 1

parts:
  U1 = L298 [package=multiwatt15]
  C1 = Ceramic Capacitor [capacitance=47µF part_number=445-8441-ND package="100 mil [THT, multilayer]"]
  VCC1 = Battery
  C2 = Ceramic Capacitor [capacitance=47µF part_number=445-8441-ND package="100 mil [THT, multilayer]"]
  D1 = Rectifier Diode [part_number=1N4002 package="300 mil [THT]"]
  D2 = Rectifier Diode [part_number=1N4002 package="300 mil [THT]"]
  D3 = Rectifier Diode [part_number=1N4002 package="300 mil [THT]"]
  D4 = Rectifier Diode [part_number=1N4002 package="300 mil [THT]"]
  D5 = Rectifier Diode [part_number=1N4002 package="300 mil [THT]"]
  D6 = Rectifier Diode [part_number=1N4002 package="300 mil [THT]"]
  D7 = Rectifier Diode [part_number=1N4002 package="300 mil [THT]"]
  D8 = Rectifier Diode [part_number=1N4002 package="300 mil [THT]"]
  M1 = DC Motor
  M2 = DC Motor
  J1 = female pin header, 1 pin [form="♀ (female)"]
  J2 = female pin header, 1 pin [form="♀ (female)"]
  J3 = female pin header, 1 pin [form="♀ (female)"]
  J4 = female pin header, 1 pin [form="♀ (female)"]
  Part1 = Arduino Nano (Rev3.0)

nets:
  N1: U1.CSA, U1.GND, U1.CSB, C1.0, VCC1.-, C2.0, D2.anode, D4.anode, D5.anode
  N2: U1.OUT1, D1.anode, D2.cathode, M1.pin_1, J1.pin1
  N3: U1.OUT2, D4.cathode, D7.anode, M1.pin_2, J2.pin1
  N4: U1.VS, C1.1, D1.cathode, D7.cathode, D8.cathode
  N5: U1.IN1, Part1.D7
  N6: U1.ENA, Part1.D2
  N7: U1.IN2, C2.1, Part1.D6
  N8: U1.VLS, VCC1.+
  N9: U1.IN3, Part1.D4
  N10: U1.ENB, Part1.D5
  N11: U1.IN4, Part1.D3
  N12: U1.OUT3, D5.cathode, D8.anode, M2.pin_2, J4.pin1
  N13: U1.OUT4, D3.anode, D6.cathode, M2.pin_1, J3.pin1

notes:
  Arduino pin allocation:
  D2: motor 0 enable
  D3: motor 0 A
  D4: motor 0 B
  D5: motor 1 enable
  D6: motor 1 A
  D7: motor 1 B
